// Logisim project MCU.circ as structural Verilog
module MCU (
  input  [4:0] KBD_command,
  input  [10:0] KBD_energy_increment,
  input  KBD_Ready,
  input  MISO,
  input  SPI_busy,
  input  Reset,
  input  CLK,
  output Request_KBD_command,
  output Request_KBD_energy,
  output [7:0] Cell_CSC,
  output [7:0] Cell_CSR,
  output SPI_clock,
  output MOSI,
  output [2:0] Table_CSC,
  output [5:0] Table_CSR,
  output Task_CS,
  output Waiting_IO,
  output SPI_communication_in_progress
);

  wire and_1_out, and_2_out, and_3_out, cdm_8_1_data_code_prime, cdm_8_1_load_st_prime, cdm_8_1_mem, Data,
       decoder_1_out0, not_1_out, spi_module_master_1_communication_end,
       spi_module_master_1_input_transanction_end, spi_module_master_1_output_transanction_end, undriven;
  wire [7:0] cdm_8_1_addr, cdm_8_1_data_out, cdm_8_1_pc, cdm_8_1_ps, cdm_8_1_r0, cdm_8_1_r1, cdm_8_1_r2,
       cdm_8_1_r3, cdm_8_1_sp, controlled_buffer_1_out, controlled_buffer_2_out, register_1_q, register_4_q;

  // Probe on cdm_8_1_r0
  // Probe on cdm_8_1_r0
  // Probe on cdm_8_1_r0
  // Probe on cdm_8_1_ps[6:4]
  // Probe on cdm_8_1_ps[7]
  // Probe on cdm_8_1_pc
  // Probe on cdm_8_1_r1
  // Probe on cdm_8_1_r0
  // Probe on cdm_8_1_ps[2]
  // Probe on cdm_8_1_ps[3]
  // Probe on cdm_8_1_r1
  // Probe on cdm_8_1_r1
  // Probe on cdm_8_1_r1
  // Probe on cdm_8_1_ps[0]
  // Probe on cdm_8_1_ps[1]
  // Probe on cdm_8_1_r2
  // Probe on cdm_8_1_r2
  // Probe on cdm_8_1_r2
  // Probe on cdm_8_1_r2
  // Probe on cdm_8_1_sp
  // Probe on cdm_8_1_r3
  // Probe on cdm_8_1_r3
  // Probe on cdm_8_1_r3
  // Probe on cdm_8_1_r3
  CdM_8 cdm_8_1 (
    .data_code_prime(cdm_8_1_data_code_prime), .R0(cdm_8_1_r0), .R1(cdm_8_1_r1), .mem(cdm_8_1_mem),
    .R2(cdm_8_1_r2), .load_st_prime(cdm_8_1_load_st_prime), .R3(cdm_8_1_r3), .addr(cdm_8_1_addr),
    .PC(cdm_8_1_pc), .SP(cdm_8_1_sp), .data_out(cdm_8_1_data_out), .data_in(controlled_buffer_2_out),
    .PS(cdm_8_1_ps), .clk(CLK), .rset(Reset));  // open: page, IAck, IRQ, vector, shadow
  Decoder #(.disabled(0)) decoder_1 (
    .out0(decoder_1_out0), .out1(Data), .sel(cdm_8_1_data_code_prime), .en(cdm_8_1_mem));
  assign controlled_buffer_1_out = not_1_out ? cdm_8_1_data_out : 8'bz;  // Controlled_Buffer controlled_buffer_1
  not not_1 (not_1_out, cdm_8_1_load_st_prime);
  assign controlled_buffer_2_out = cdm_8_1_load_st_prime ? controlled_buffer_1_out : 8'bz;  // Controlled_Buffer controlled_buffer_2
  and and_1 (and_1_out, ~and_2_out, Data);  // AND_Gate
  and and_2 (and_2_out, cdm_8_1_addr[0], cdm_8_1_addr[1], cdm_8_1_addr[2], cdm_8_1_addr[3], cdm_8_1_addr[4], cdm_8_1_addr[5], cdm_8_1_addr[6], cdm_8_1_addr[7], ~cdm_8_1_load_st_prime);  // AND_Gate
  ROM rom_1 (.addr(cdm_8_1_addr), .data(controlled_buffer_1_out), .sel(decoder_1_out0));
  RAM ram_1 (
    .addr(cdm_8_1_addr), .data(controlled_buffer_1_out), .sel(and_1_out), .clk(CLK),
    .ld(cdm_8_1_load_st_prime), .clr(1'b0));
  Register #(.trigger("falling")) register_1 (
    .D(controlled_buffer_1_out), .en(and_2_out), .Q(register_1_q), .clk(CLK), .clr(1'b0));
  Register #(.trigger("falling")) register_2 (
    .D(controlled_buffer_1_out), .Q(Cell_CSC), .clk(CLK), .clr(Reset));  // open: en
  Register #(.trigger("falling")) register_3 (
    .D(controlled_buffer_1_out), .Q(Cell_CSR), .clk(CLK), .clr(Reset));  // open: en
  Register #(.trigger("falling")) register_4 (.Q(register_4_q), .clk(undriven), .clr(Reset));  // open: D, en
  and and_3 (and_3_out, CLK, ~SPI_busy);  // AND_Gate
  LED led_1 (.in(spi_module_master_1_output_transanction_end));
  LED led_2 (.in(spi_module_master_1_input_transanction_end));
  SPI_module__master spi_module_master_1 (
    .In_clock(and_3_out), .MISO(MISO), .CLK(SPI_clock), .MOSI(MOSI),
    .Output_transanction_end(spi_module_master_1_output_transanction_end),
    .Input_transanction_end(spi_module_master_1_input_transanction_end), .Control_command(register_4_q),
    .Communication_end(spi_module_master_1_communication_end));  // open: Send_command, Send_energy, Recv_data
  LED led_3 (.in(spi_module_master_1_communication_end));
endmodule

module IO_dmx (
  input  [7:0] Address
);
endmodule
